// Logisim project 4Bit_BCD_AdderSubtractor.circ as structural Verilog: 1 circuit, main circuit main
module main (
  input  in_1,
  input  in_2,
  input  in_3,
  input  in_4,
  input  in_5,
  input  in_6,
  input  in_7,
  input  in_8,
  input  in_9,
  output out_10,
  output out_11,
  output out_12,
  output out_13,
  output out_14,
  output out_15,
  output out_16,
  output out_17,
  output [3:0] out_18,
  output [3:0] out_19,
  output [3:0] out_20,
  output [3:0] out_21
);

  wire and_1_out, and_2_out, and_3_out, and_4_out, and_5_out, and_6_out, and_7_out, and_8_out, and_9_out,
       and_10_out, and_11_out, and_14_out, and_15_out, and_16_out, and_17_out, and_18_out, and_19_out,
       and_20_out, and_21_out, B, C, K, n7447_1_pin3, n7447_2_pin3, n7447_3_pin3, not_1_out, notB, notK,
       notT, or_1_out, or_2_out, or_3_out, or_5_out, or_7_out, or_8_out, or_9_out, or_10_out, Sa, Sb, Sc, Sd,
       Se, Sf, Sg, T, Xa, Xb, Xc, Xd, Xe, Xf, Xg, xor_1_out, xor_2_out, xor_3_out, xor_4_out, xor_5_out,
       xor_6_out, xor_7_out, xor_8_out, xor_13_out, xor_14_out, xor_15_out, xor_16_out, xor_17_out,
       xor_18_out, xor_19_out, xor_20_out, Ya, Yb, Yc, Yd, Ye, Yf, Yg;

  xor xor_1 (xor_1_out, in_9, in_8);
  xor xor_2 (xor_2_out, in_9, in_7);
  xor xor_3 (xor_3_out, in_9, in_6);
  xor xor_4 (xor_4_out, in_9, in_5);
  xor xor_5 (xor_5_out, in_4, xor_1_out);
  xor xor_6 (xor_6_out, in_3, xor_2_out);
  xor xor_7 (xor_7_out, in_2, xor_3_out);
  xor xor_8 (xor_8_out, in_1, xor_4_out);
  xor xor_9 (out_13, xor_5_out, in_9);
  and and_1 (and_1_out, in_9, xor_5_out);
  and and_2 (and_2_out, in_4, xor_1_out);
  xor xor_10 (out_12, xor_6_out, or_1_out);
  and and_3 (and_3_out, or_1_out, xor_6_out);
  and and_4 (and_4_out, in_3, xor_2_out);
  xor xor_11 (out_11, xor_7_out, or_2_out);
  and and_5 (and_5_out, or_2_out, xor_7_out);
  and and_6 (and_6_out, in_2, xor_3_out);
  xor xor_12 (out_10, xor_8_out, or_3_out);
  and and_7 (and_7_out, or_3_out, xor_8_out);
  and and_8 (and_8_out, in_1, xor_4_out);
  or or_1 (or_1_out, and_1_out, and_2_out);
  or or_2 (or_2_out, and_3_out, and_4_out);
  or or_3 (or_3_out, and_5_out, and_6_out);
  or or_4 (K, and_7_out, and_8_out);
  and and_9 (and_9_out, out_11, out_12);
  _7_Segment_Display #(.active("false"), .decimalPoint("false")) u_7_segment_display_1 (
    .g(Xg), .f(Xf), .a(Xa), .b(Xb), .e(Xe), .d(Xd), .c(Xc));
  or or_5 (or_5_out, out_10, and_9_out);
  _7_Segment_Display #(.active("false"), .decimalPoint("false")) u_7_segment_display_2 (
    .g(Yg), .f(Yf), .a(Ya), .b(Yb), .e(Ye), .d(Yd), .c(Yc));
  and and_10 (and_10_out, out_12, out_10);
  and and_11 (and_11_out, out_11, out_10);
  and and_12 (T, in_9, notK, or_5_out);
  or or_6 (C, and_10_out, and_11_out, K);
  _7_Segment_Display #(.active("false"), .decimalPoint("false")) u_7_segment_display_3 (
    .g(notT), .f(1'b1), .a(1'b1), .b(notB), .e(1'b1), .d(1'b1), .c(notB));
  _7447 u_7447_1 (
    .pin1(in_3), .pin2(in_2), .pin3(n7447_1_pin3), .pin4(n7447_1_pin3), .pin5(n7447_1_pin3), .pin6(in_1),
    .pin7(in_4), .pin15(Xf), .pin14(Xg), .pin13(Xa), .pin12(Xb), .pin11(Xc), .pin10(Xd), .pin9(Xe));
  _7447 u_7447_2 (
    .pin1(in_7), .pin2(in_6), .pin3(n7447_2_pin3), .pin4(n7447_2_pin3), .pin5(n7447_2_pin3), .pin6(in_5),
    .pin7(in_8), .pin15(Yf), .pin14(Yg), .pin13(Ya), .pin12(Yb), .pin11(Yc), .pin10(Yd), .pin9(Ye));
  _7447 u_7447_3 (
    .pin1(out_16), .pin2(out_15), .pin3(n7447_3_pin3), .pin4(n7447_3_pin3), .pin5(n7447_3_pin3),
    .pin6(out_14), .pin7(out_17), .pin15(Sf), .pin14(Sg), .pin13(Sa), .pin12(Sb), .pin11(Sc), .pin10(Sd),
    .pin9(Se));
  not not_1 (not_1_out, in_9);
  and and_13 (B, not_1_out, C);
  _7_Segment_Display #(.active("false"), .decimalPoint("false")) u_7_segment_display_4 (
    .g(Sg), .f(Sf), .a(Sa), .b(Sb), .e(Se), .d(Sd), .c(Sc));
  not not_2 (notK, K);
  not not_3 (notT, T);
  not not_4 (notB, B);
  xor xor_13 (xor_13_out, T, out_13);
  xor xor_14 (xor_14_out, T, out_12);
  xor xor_15 (xor_15_out, T, out_11);
  xor xor_16 (xor_16_out, T, out_10);
  xor xor_17 (xor_17_out, 1'b0, xor_13_out);
  xor xor_18 (xor_18_out, B, xor_14_out);
  xor xor_19 (xor_19_out, B, xor_15_out);
  xor xor_20 (xor_20_out, 1'b0, xor_16_out);
  xor xor_21 (out_17, xor_17_out, T);
  and and_14 (and_14_out, T, xor_17_out);
  or or_7 (or_7_out, and_14_out, and_15_out);
  and and_15 (and_15_out, 1'b0, xor_13_out);
  xor xor_22 (out_16, xor_18_out, or_7_out);
  and and_16 (and_16_out, or_7_out, xor_18_out);
  or or_8 (or_8_out, and_16_out, and_17_out);
  and and_17 (and_17_out, B, xor_14_out);
  xor xor_23 (out_15, xor_19_out, or_8_out);
  and and_18 (and_18_out, or_8_out, xor_19_out);
  or or_9 (or_9_out, and_18_out, and_19_out);
  and and_19 (and_19_out, B, xor_15_out);
  xor xor_24 (out_14, xor_20_out, or_9_out);
  and and_20 (and_20_out, or_9_out, xor_20_out);
  or or_10 (or_10_out, and_20_out, and_21_out);
  and and_21 (and_21_out, 1'b0, xor_16_out);

  assign out_18 = {in_1, in_2, in_3, in_4};
  assign out_19 = {in_5, in_6, in_7, in_8};
  assign out_20 = {out_10, out_11, out_12, out_13};
  assign out_21 = {out_14, out_15, out_16, out_17};
  // also tied to VCC on the sheet: {n7447_1_pin3, n7447_2_pin3, n7447_3_pin3}

  // Other names for the same wires on the sheet: M = in_9; X0 = in_4; X1 = in_3; X2 = in_2; X3 = in_1; Y0 = in_8;
  //   Y1 = in_7; Y2 = in_6; Y3 = in_5; Z0 = out_13; Z1 = out_12; Z2 = out_11; Z3 = out_10; S0 = out_17; S1 = out_16;
  //   S2 = out_15; S3 = out_14
endmodule
